# Fritzing sketch shield (saved by Fritzing 0.9.2b)
circuit board: 6.87439cm x 5.41746cm
breadboards: 1

parts:
  Table_Ctrl = Arduino Uno (Rev3)
  10K = Resistor [tolerance=±5% resistance=10k package=THT]
  10K_2 = Resistor [tolerance=±5% resistance=10k package=THT]
  Table_Board = LG_FPC_10_1mm
  RL1 = relay d2a050000
  RL0 = relay d2a050000
  SPKR = Piezo Speaker
  Sensor = 4pin connector sideways
  Buttons = 4pin connector sideways

nets:
  N1: Table_Ctrl.D11_PWM/MOSI, 10K_2.Pin_1, Buttons.pin2
  N2: Table_Ctrl.D12/MISO, 10K.Pin_1, Buttons.pin1
  N3: Table_Ctrl.GND, 10K.Pin_0, 10K_2.Pin_0, RL1.pin6, RL0.pin6, SPKR.pin1, Sensor.pin0, Buttons.pin0
  N4: Table_Ctrl.D2, Sensor.pin2
  N5: Table_Ctrl.D3_PWM, Sensor.pin1
  N6: Table_Ctrl.D5_PWM, SPKR.pin2
  N7: Table_Ctrl.D6_PWM, RL1.pin2
  N8: Table_Ctrl.D7, RL0.pin2
  N9: Table_Ctrl.5V, Sensor.pin3
  N10: Table_Board.pin_4, RL1.pin1, RL0.pin1
  N11: Table_Board.pin_5, RL1.pin7
  N12: Table_Board.pin_6, RL0.pin7

custom parts:
  LG_FPC_10_1mm: würth ffc/fpc 10 connector x 1mm raster
